// Digital circuit ALU.dig as structural Verilog
module ALU (
  input  [7:0] inbus,
  input  [1:0] op
);

  Driver #(.Bits(8)) driver_1 (.in(inbus));  // open: en, out
  // ALU_CU alu_cu_1: pin names not known; wires that end beside it: op
endmodule
